# Fritzing sketch Project_A_Skecth (saved by Fritzing 0.9.10b)
breadboards: 1

parts:
  VCC1 = Battery block 9V  # not connected
  Mod1 = Raspberry Pi 4B
  M1 = gear-motor  # not connected
  M2 = gear-motor  # not connected
  M3 = gear-motor  # not connected
  M4 = gear-motor  # not connected
  Bauteil2 = Motor Driver 1A Dual TB6612FNG  # not connected
  Bauteil3 = Motor Driver 1A Dual TB6612FNG
  Bauteil4 = Motor Driver 1A Dual TB6612FNG  # not connected

nets:
  N1: Mod1.GPIO12, Bauteil3.PWMA

notes:
  Motor: U_L
  Motor: U_R
  Motor: B_R
  Motor: B_L
